# Fritzing sketch lancer (saved by Fritzing 0.9.3b)

parts:
  Part1 = 12-Channel 16-bit PWM LED Driver - SPI [part_number=1455]
  Part2 = Adafruit Trinket 3V [part_number="Adafruit #1500"]
  S1 = Momentary Switch [package=tactile-pth]
  JP1 = Header 2 [package=jst-2-smd]
  R1 = Resistor [tolerance=±5% resistance=47k package="2512 [SMD]"]

nets:
  N1: Part1.V+, Part2.VBAT
  GND: Part1.GND, Part2.GND, JP1.1, R1.Pin_0
  N2: Part1.DI, Part2.#0
  N3: Part1.CI, Part2.#2
  VCC: Part1.VCC, Part2.+3V3
  N4: Part2.#4, S1.4, R1.Pin_1
  N5: Part2.#3, S1.3

custom parts:
  12-Channel 16-bit PWM LED Driver - SPI: This chip can control 12 separate channels of 16-bit PWM output. This is the highest-resolution PWM board we've seen! Designed (and ideal) for precision LED control, this board is NOT good for driving servos. Only two "SPI" pins are required to send data, and the design is completely chainable. As long as there's enough power for all the boards you can chain as many as you'd like.
  Adafruit Trinket 3V: Trinket may be small, but do not be fooled by its size! It's a tiny microcontroller board, built around the Atmel ATtiny85, a little chip with a lot of power. We wanted to design a microcontroller board that was small enough to fit into any project, and low cost enough to use without hesitation. Perfect for when you don't want to give up your expensive dev-board and you aren't willing to take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
